// Logisim project ClubDeToby.circ as structural Verilog: 1 circuit, main circuit main
module main (
  input  W,
  input  X,
  input  Y,
  input  Z,
  output out_5
);

  wire and_1_out, and_2_out, and_3_out, and_4_out, and_5_out, or_1_out, or_2_out;

  and and_1 (and_1_out, W, X);
  and and_2 (and_2_out, Y, W);
  and and_3 (and_3_out, Z, W);
  and and_4 (and_4_out, X, Y);
  or or_1 (or_1_out, and_2_out, and_3_out);
  and and_5 (and_5_out, and_4_out, Z);
  or or_2 (or_2_out, and_1_out, and_5_out);
  or or_3 (out_5, or_2_out, or_1_out);

  // Notes on the sheet:
  //   WX
  //   WY
  //   WZ
  //   XY
  //   WY + WZ
  //   XYZ
  //   WX + XYZ
  //   WX + XYZ + WY + WZ
  //   ¡SI PRENDE ES PORQUE COMPRAN CHOCOLATES!
endmodule
